# Fritzing sketch circuit (saved by Fritzing 0.9.1b)

parts:
  12V/5A_power_supply = Power plug
  Arduino = Arduino Uno (Rev3)
  12V_Relay = Keyes Relay [package=THT]
  5A_fuse = FUSE [package=fuse_5mm]
  5A_fuse_2 = FUSE [package=fuse_5mm]
  12V_Water_Pump = DC Motor
  LED1 = LED - 5mm [color="Red (633nm)" package="5 mm [THT]"]
  R1 = Resistor [tolerance=±5% resistance=220 package=THT]
  Signal_switch = SWITCH-SPST-2 [package=switch-spst-vertical]
  LED2 = LED - 5mm [color="Red (633nm)" package="5 mm [THT]"]
  R2 = Resistor [tolerance=±5% resistance=220 package=THT]
  R3 = Resistor [tolerance=±5% resistance=220 package=THT]
  LED3 = LED - 5mm [color="Red (633nm)" package="5 mm [THT]"]

nets:
  N1: 12V/5A_power_supply.GND, 5A_fuse_2.1
  N2: 12V/5A_power_supply.VCC, 5A_fuse.1
  N3: Arduino.GND, 12V_Relay.ground, LED1.cathode, Signal_switch.P, LED2.cathode, LED3.cathode
  N4: Arduino.D2, Signal_switch.O
  N5: Arduino.D3_PWM, 12V_Relay.signal
  N6: Arduino.D4, R1.Pin_0
  N7: Arduino.D5_PWM, R2.Pin_0
  N8: Arduino.D6_PWM, R3.Pin_0
  N9: Arduino.5V, 12V_Relay.power
  N10: 12V_Relay.C, 5A_fuse.2
  N11: 12V_Relay.NO, 12V_Water_Pump.pin_2
  N12: 5A_fuse_2.2, 12V_Water_Pump.pin_1
  N13: LED1.anode, R1.Pin_1
  N14: LED2.anode, R2.Pin_1
  N15: R3.Pin_1, LED3.anode

notes:
  a 12V/5A water pump
  5A fuses
  12V/5A power supply

custom parts:
  Keyes Relay: The Keyes 5V relay module is suitable for SCM development, home appliance control. It uses a 5V~12V TIL control signal which can control DC / AC signal.
